// Logisim project circuito_cpu.circ as structural Verilog
module main (
);

  wire alu_block_aux_br, alu_br, alu_src, br, branch_en_out, clk, EX_MEM_reg_mem_r_out,
       EX_MEM_reg_mem_to_reg_out, EX_MEM_reg_mem_w_out, EX_MEM_reg_reg_w_out, fwd_c, ID_EX_br_in,
       ID_EX_pc_reg_br, ID_EX_reg_alu_src_out, ID_EX_reg_branch_out, ID_EX_reg_mem_r_out,
       ID_EX_reg_mem_to_reg_out, ID_EX_reg_mem_w_out, ID_EX_reg_pc_reg_alu_out, ID_EX_reg_pc_reg_br_out,
       ID_EX_reg_reg_w_out, mem_r, mem_reg, mem_w, MEM_WB_reg_mem_to_reg_out, MEM_WB_reg_reg_w_out,
       pc_reg_alu, pc_reg_br, subctrlsys_reg_write;
  wire [1:0] fwd_a, fwd_b;
  wire [2:0] alu_op, ID_EX_reg_alu_op_out;
  wire [3:0] alu_ctrl_sys_opcode;
  wire [4:0] EX_MEM_reg_wb_addr_out, ID_EX_reg_instr_out_2, ID_EX_reg_instr_out_3, MEM_WB_reg_wb_addr_out;
  wire [31:0] alu_block_out_r, EX_MEM_alu_result, EX_MEM_reg_imm_out, EX_MEM_reg_pc_out,
       EX_MEM_reg_reg_a_out, EX_MEM_reg_reg_b_out, ID_EX_imm, ID_EX_pc, ID_EX_reg_a, ID_EX_reg_b,
       ID_EX_reg_instr_out, IF_ID_pc, IF_ID_reg_instr_out, immediate_gen_imm, MEM_WB_reg_alu_result_out,
       MEM_WB_reg_mem_out, MEM_WB_result, multiplexer_1_out, multiplexer_2_out, multiplexer_3_out,
       multiplexer_4_out, prog_count_1_pc, program_mem_data, reg_b_ex_mem_in, register_file_reg_a_data,
       register_file_reg_b_data;

  and branch_en (branch_en_out, alu_br, br);
  prog_count prog_count_1 (
    .clk(clk), .imm(EX_MEM_reg_imm_out), .branch(branch_en_out), .pc_reg_mux(pc_reg_br),
    .reg_in(EX_MEM_reg_reg_a_out), .pc_in(EX_MEM_reg_pc_out), .pc(prog_count_1_pc));
  ROM #(.addrWidth(24), .dataWidth(32)) program_mem (.addr(prog_count_1_pc[23:0]), .data(program_mem_data));
  IF_ID IF_ID_reg (
    .clk(clk), .instr_in(program_mem_data), .pc_in(prog_count_1_pc), .instr_out(IF_ID_reg_instr_out),
    .pc_out(IF_ID_pc));
  ctrl_unit subctrlsys (
    .instr(IF_ID_reg_instr_out), .pc_reg(pc_reg_alu), .alu_op(alu_op), .branch(ID_EX_br_in),
    .mem_read(mem_r), .mem_write(mem_w), .mem_to_reg(mem_reg), .alu_src(alu_src),
    .reg_write(subctrlsys_reg_write), .pc_reg_branch(ID_EX_pc_reg_br));
  reg_file register_file (
    .clk(clk), .write_en(MEM_WB_reg_reg_w_out), .write_data(MEM_WB_result),
    .write_addr(MEM_WB_reg_wb_addr_out), .reg_a_addr(IF_ID_reg_instr_out[19:15]),
    .reg_b_addr(IF_ID_reg_instr_out[24:20]), .reg_a_data(register_file_reg_a_data),
    .reg_b_data(register_file_reg_b_data));
  imm_gen immediate_gen (.instr(IF_ID_reg_instr_out), .imm(immediate_gen_imm));
  ID_EX ID_EX_reg (
    .clk(clk), .instr_in(IF_ID_reg_instr_out), .pc_in(IF_ID_pc), .reg_a_in(register_file_reg_a_data),
    .reg_b_in(register_file_reg_b_data), .imm_in(immediate_gen_imm), .pc_reg_alu_in(pc_reg_alu),
    .alu_src_in(alu_src), .alu_op_in(alu_op), .mem_w_in(mem_w), .mem_r_in(mem_r), .branch_in(ID_EX_br_in),
    .pc_reg_br_in(ID_EX_pc_reg_br), .mem_to_reg_in(mem_reg), .reg_w_in(subctrlsys_reg_write),
    .instr_out({ID_EX_reg_instr_out[31:25], ID_EX_reg_instr_out_3, ID_EX_reg_instr_out_2, ID_EX_reg_instr_out[14:0]}),
    .pc_out(ID_EX_pc), .reg_a_out(ID_EX_reg_a), .reg_b_out(ID_EX_reg_b), .imm_out(ID_EX_imm),
    .pc_reg_alu_out(ID_EX_reg_pc_reg_alu_out), .alu_src_out(ID_EX_reg_alu_src_out),
    .alu_op_out(ID_EX_reg_alu_op_out), .mem_w_out(ID_EX_reg_mem_w_out), .mem_r_out(ID_EX_reg_mem_r_out),
    .branch_out(ID_EX_reg_branch_out), .pc_reg_br_out(ID_EX_reg_pc_reg_br_out),
    .mem_to_reg_out(ID_EX_reg_mem_to_reg_out), .reg_w_out(ID_EX_reg_reg_w_out));
  Clock clk_src (.out(clk));
  Multiplexer #(.enable("false"), .select(2), .width(32)) multiplexer_1 (
    .in0(ID_EX_reg_a), .in1(MEM_WB_result), .in2(EX_MEM_alu_result), .in3({32{1'b0}}),
    .out(multiplexer_1_out), .sel(fwd_a));
  Multiplexer #(.enable("false"), .select(2), .width(32)) multiplexer_2 (
    .in0(ID_EX_reg_b), .in1(MEM_WB_result), .in2(EX_MEM_alu_result), .in3({32{1'b0}}),
    .out(multiplexer_2_out), .sel(fwd_b));
  alu_ctrl alu_ctrl_sys (
    .alu_op(ID_EX_reg_alu_op_out),
    .instruction({ID_EX_reg_instr_out[31:25], ID_EX_reg_instr_out_3, ID_EX_reg_instr_out_2, ID_EX_reg_instr_out[14:0]}),
    .opcode(alu_ctrl_sys_opcode));
  Multiplexer #(.enable("false"), .width(32)) multiplexer_3 (
    .in0(multiplexer_1_out), .in1(ID_EX_pc), .out(multiplexer_3_out), .sel(ID_EX_reg_pc_reg_alu_out));
  Multiplexer #(.enable("false"), .width(32)) multiplexer_4 (
    .in0(multiplexer_2_out), .in1(ID_EX_imm), .out(multiplexer_4_out), .sel(ID_EX_reg_alu_src_out));
  alu alu_block (
    .in_a(multiplexer_3_out), .in_b(multiplexer_4_out), .op(alu_ctrl_sys_opcode), .out_r(alu_block_out_r),
    .aux_br(alu_block_aux_br));
  fwd_unit forwarding_unit (
    .reg_s1(ID_EX_reg_instr_out_2), .reg_s2(ID_EX_reg_instr_out_3), .reg_dst(ID_EX_reg_instr_out[11:7]),
    .mem_wb_reg_dst(MEM_WB_reg_wb_addr_out), .ex_mem_reg_dst(EX_MEM_reg_wb_addr_out),
    .ex_mem_reg_w(EX_MEM_reg_reg_w_out), .mem_wb_reg_w(MEM_WB_reg_reg_w_out), .forward_a(fwd_a),
    .forward_b(fwd_b), .forward_c(fwd_c));
  Multiplexer #(.enable("false"), .width(32)) multiplexer_5 (
    .in0(ID_EX_reg_b), .in1(EX_MEM_alu_result), .out(reg_b_ex_mem_in), .sel(fwd_c));
  EX_MEM EX_MEM_reg (
    .clk(clk), .alu_result_in(alu_block_out_r), .branch_alu_in(alu_block_aux_br), .reg_a_in(ID_EX_reg_a),
    .reg_b_in(reg_b_ex_mem_in), .imm_in(ID_EX_imm), .wb_addr_in(ID_EX_reg_instr_out[11:7]), .pc_in(ID_EX_pc),
    .mem_w_in(ID_EX_reg_mem_w_out), .mem_r_in(ID_EX_reg_mem_r_out), .branch_in(ID_EX_reg_branch_out),
    .pc_reg_br_in(ID_EX_reg_pc_reg_br_out), .mem_to_reg_in(ID_EX_reg_mem_to_reg_out),
    .reg_w_in(ID_EX_reg_reg_w_out), .imm_out(EX_MEM_reg_imm_out), .reg_a_out(EX_MEM_reg_reg_a_out),
    .reg_b_out(EX_MEM_reg_reg_b_out), .alu_result_out(EX_MEM_alu_result), .branch_alu_out(alu_br),
    .wb_addr_out(EX_MEM_reg_wb_addr_out), .pc_out(EX_MEM_reg_pc_out), .mem_w_out(EX_MEM_reg_mem_w_out),
    .mem_r_out(EX_MEM_reg_mem_r_out), .branch_out(br), .pc_reg_br_out(pc_reg_br),
    .mem_to_reg_out(EX_MEM_reg_mem_to_reg_out), .reg_w_out(EX_MEM_reg_reg_w_out));
  RAM #(.addrWidth(24), .dataWidth(32), .databus("bidir"), .enables("line"), .trigger("falling")) data_mem (
    .addr(EX_MEM_alu_result[23:0]), .we(EX_MEM_reg_mem_w_out), .oe(EX_MEM_reg_mem_r_out), .clk(clk),
    .data(EX_MEM_reg_reg_b_out));
  MEM_WB MEM_WB_reg (
    .clk(clk), .alu_result_in(EX_MEM_alu_result), .mem_in(EX_MEM_reg_reg_b_out),
    .wb_addr_in(EX_MEM_reg_wb_addr_out), .mem_to_reg_in(EX_MEM_reg_mem_to_reg_out),
    .reg_w_in(EX_MEM_reg_reg_w_out), .alu_result_out(MEM_WB_reg_alu_result_out),
    .mem_out(MEM_WB_reg_mem_out), .wb_addr_out(MEM_WB_reg_wb_addr_out),
    .mem_to_reg_out(MEM_WB_reg_mem_to_reg_out), .reg_w_out(MEM_WB_reg_reg_w_out));
  Multiplexer #(.enable("false"), .width(32)) multiplexer_6 (
    .in0(MEM_WB_reg_alu_result_out), .in1(MEM_WB_reg_mem_out), .out(MEM_WB_result),
    .sel(MEM_WB_reg_mem_to_reg_out));

  // Notes on the sheet:
  //   contents of program_mem (hex, n*v repeats v):
  //   7ff00313 7ff30313 130313 c00613 c313b3 6383b3 333 7002b3 532023 130313 fe731ee3 7ff00313 7ff30313
  //   130313 c00613 c313b3 6383b3 333 7002b3 532023 130313 fe731ee3 7ff00313 7ff30313 130313 c00613 c313b3
  //   6383b3 333 7002b3 532023 130313 fe731ee3 7ff00313 7ff30313 130313 c00613 c313b3 6383b3 333 7002b3
  //   532023 130313 fe731ee3 7ff00313 7ff30313 130313 c00613 c313b3 6383b3 333 7002b3 532023 130313
  //   fe731ee3 7ff00313 7ff30313 130313 c00613 c313b3 6383b3 333 7002b3 532023 130313 fe731ee3 7ff00313
  //   7ff30313 130313 c00613 c313b3 6383b3 333 7002b3 532023 130313 fe731ee3 7ff00313 7ff30313 130313
  //   c00613 c313b3 6383b3 333 7002b3 532023 130313 fe731ee3 7ff00313 7ff30313 130313 c00613 c313b3 6383b3
  //   333 7002b3 532023 130313 fe731ee3 7ff00313 7ff30313 130313 c00613 c313b3 6383b3 333 7002b3 532023
  //   130313 fe731ee3 7ff00313 7ff30313 130313 c00613 c313b3 6383b3 333 7002b3 532023 130313 fe731ee3
  //   7ff00313 7ff30313 130313 c00613 c313b3 6383b3 333 7002b3 532023 130313 fe731ee3 7ff00313 7ff30313
  //   130313 c00613 c313b3 6383b3 333 7002b3 532023 130313 fe731ee3 7ff00313 7ff30313 130313 c00613 c313b3
  //   6383b3 333 7002b3 532023 130313 fe731ee3 7ff00313 7ff30313 130313 c00613 c313b3 6383b3 333 7002b3
  //   532023 130313 fe731ee3 7ff00313 7ff30313 130313 c00613 c313b3 6383b3 333 7002b3 532023 130313
  //   fe731ee3 7ff00313 7ff30313 130313 c00613 c313b3 6383b3 333 7002b3 532023 130313 fe731ee3 7ff00313
  //   7ff30313 130313 c00613 c313b3 6383b3 333 7002b3 532023 130313 fe731ee3 7ff00313 7ff30313 130313
  //   c00613 c313b3 6383b3 333 7002b3 532023 130313 fe731ee3 7ff00313 7ff30313 130313 c00613 c313b3 6383b3
  //   333 7002b3 532023 130313 fe731ee3 7ff00313 7ff30313 130313 c00613 c313b3 6383b3 333 7002b3 532023
  //   130313 fe731ee3 7ff00313 7ff30313 130313 c00613 c313b3 6383b3 333 7002b3 532023 130313 fe731ee3
  //   7ff00313 7ff30313 130313 c00613 c313b3 6383b3 333 7002b3 532023 130313 fe731ee3 7ff00313 7ff30313
  //   130313 c00613 c313b3 6383b3 333 7002b3 532023 130313 fe731ee3 7ff00313 7ff30313 130313 c00613 c313b3
  //   6383b3 333 7002b3 532023 130313 fe731ee3 7ff00313 7ff30313 130313 c00613 c313b3 6383b3 333 7002b3
  //   532023 130313 fe731ee3 7ff00313 7ff30313 130313 c00613 c313b3 6383b3 333 7002b3 532023 130313
  //   fe731ee3 7ff00313 7ff30313 130313 c00613 c313b3 6383b3 333 7002b3 532023 130313 fe731ee3 7ff00313
  //   7ff30313 130313 c00613 c313b3 6383b3 333 7002b3 532023 130313 fe731ee3 7ff00313 7ff30313 130313
  //   c00613 c313b3 6383b3 333 7002b3 532023 130313 fe731ee3 7ff00313 7ff30313 130313 c00613 c313b3 6383b3
  //   333 7002b3 532023 130313 fe731ee3 7ff00313 7ff30313 130313 c00613 c313b3 6383b3 333 7002b3 532023
  //   130313 fe731ee3 7ff00313 7ff30313 130313 c00613 c313b3 6383b3 333 7002b3 532023 130313 fe731ee3
  //   7ff00313 7ff30313 130313 c00613 c313b3 6383b3 333 7002b3 532023 130313 fe731ee3 7ff00313 7ff30313
  //   130313 c00613 c313b3 6383b3 333 7002b3 532023 130313 fe731ee3 7ff00313 7ff30313 130313 c00613 c313b3
  //   6383b3 333 7002b3 532023 130313 fe731ee3 7ff00313 7ff30313 130313 c00613 c313b3 6383b3 333 7002b3
  //   532023 130313 fe731ee3 7ff00313 7ff30313 130313 c00613 c313b3 6383b3 333 7002b3 532023 130313
  //   fe731ee3 7ff00313 7ff30313 130313 c00613 c313b3 6383b3 333 7002b3 532023 130313 fe731ee3 7ff00313
  //   7ff30313 130313 c00613 c313b3 6383b3 333 7002b3 532023 130313 fe731ee3 7ff00313 7ff30313 130313
  //   c00613 c313b3 6383b3 333 7002b3 532023 130313 fe731ee3 7ff00313 7ff30313 130313 c00613 c313b3 6383b3
  //   333 7002b3 532023 130313 fe731ee3 7ff00313 7ff30313 130313 c00613 c313b3 6383b3 333 7002b3 532023
  //   130313 fe731ee3 7ff00313 7ff30313 130313 c00613 c313b3 6383b3 333 7002b3 532023 130313 fe731ee3
  //   7ff00313 7ff30313 130313 c00613 c313b3 6383b3 333 7002b3 532023 130313 fe731ee3 7ff00313 7ff30313
  //   130313 c00613 c313b3 6383b3 333 7002b3 532023 130313 fe731ee3 7ff00313 7ff30313 130313 c00613 c313b3
  //   6383b3 333 7002b3 532023 130313 fe731ee3 7ff00313 7ff30313 130313 c00613 c313b3 6383b3 333 7002b3
  //   532023 130313 fe731ee3 7ff00313 7ff30313 130313 c00613 c313b3 6383b3 333 7002b3 532023 130313
  //   fe731ee3 7ff00313 7ff30313 130313 c00613 c313b3 6383b3 333 7002b3 532023 130313 fe731ee3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
endmodule

// VHDL entity prog_count, as the project stores it:
library ieee;
use ieee.std_logic_1164.all;
use ieee.numeric_std.all;

entity prog_count is
    port(
        clk : in std_logic;
        imm : in std_logic_vector(31 downto 0);
        branch : in std_logic;
        pc_reg_mux : in std_logic;
        reg_in : in std_logic_vector(31 downto 0);
        pc_in : in std_logic_vector(31 downto 0);
        pc : out std_logic_vector(31 downto 0)
    );
end prog_count;

architecture Behavioral of prog_count is
    signal immediate, ptr_pc : std_logic_vector(31 downto 0) := (others => '0');
    begin
        immediate <= imm;
        pc <= ptr_pc;

        fetch_instr: process(clk, branch, pc_reg_mux, pc_in, reg_in) is
        begin
            if rising_edge(clk) then
                if branch = '1' then
                	if pc_reg_mux = '0' then
                    	ptr_pc <= std_logic_vector(signed(pc_in) + signed(immediate));
                    else
                    	ptr_pc <= std_logic_vector(signed(reg_in) + signed(immediate));
                    end if;
                else
                    ptr_pc <= std_logic_vector(unsigned(ptr_pc) + x"00000001");
                end if;
            end if;
        end process fetch_instr;
end Behavioral;

// VHDL entity reg_file, as the project stores it:
library ieee;
use ieee.std_logic_1164.all;
use ieee.numeric_std.all;

entity reg_file is
    port(
        clk : in std_logic;
        write_en : in std_logic;

        write_data : in std_logic_vector(31 downto 0);
        
        write_addr : in std_logic_vector(4 downto 0);
        reg_a_addr : in std_logic_vector(4 downto 0);
        reg_b_addr : in std_logic_vector(4 downto 0);

        reg_a_data : out std_logic_vector(31 downto 0);
        reg_b_data : out std_logic_vector(31 downto 0)
    );
end reg_file;

architecture Behavioral of reg_file is
    -- 32 registradores de 32 bits
    type register_mem is array (integer range <>) of std_logic_vector(31 downto 0);
    signal register_bank : register_mem(0 to 31) := (others => x"00000000");

    begin       
        register_access: process(clk, write_en, write_addr) is
        begin
            -- na borda de subida
            if rising_edge(clk) and write_en = '1' then
            	if write_addr /= "00000" then
            		register_bank(to_integer(unsigned(write_addr))) <= write_data;
            	end if;
            end if;
            if falling_edge(clk) then
            	reg_a_data <= register_bank(to_integer(unsigned(reg_a_addr)));
        		reg_b_data <= register_bank(to_integer(unsigned(reg_b_addr)));
            end if;
        end process register_access;

end Behavioral;

// VHDL entity imm_gen, as the project stores it:
library ieee;
use ieee.std_logic_1164.all;
use ieee.numeric_std.all;

entity imm_gen is
    port(
        instr : in std_logic_vector(31 downto 0);
        imm : out std_logic_vector(31 downto 0)
    );
end imm_gen;

architecture Behavioral of imm_gen is
begin
    decode_instr : process(instr)
    begin
        -- logica para fazer decode da instrução
        case instr(6 downto 0) is
            when "0110111" => -- lui
                imm(31 downto 12) <= instr(31 downto 12);
                imm(11 downto 0) <= (others => '0');
            when "0010111" => -- auipc
                imm(31 downto 12) <= instr(31 downto 12);
                imm(11 downto 0) <= (others => '0');
            when "1101111" => -- jal
                imm(19 downto 0) <= instr(31) & instr(19 downto 12) & instr(20) & instr(30 downto 21);
                imm(31 downto 20) <= (others => instr(31));
            when "1100111" => -- jalr
                imm(11 downto 0) <= instr(31 downto 20);
                imm(31 downto 12) <= (others => instr(31));
            when "1100011" => -- branch
                imm(11 downto 0) <= instr(31) & instr(7) & instr(30 downto 25) & instr(11 downto 8);
                imm(31 downto 12) <= (others => instr(31));
            when "0000011" => -- load
                imm(11 downto 0) <= instr(31 downto 20);
                imm(31 downto 12) <= (others => instr(31));
            when "0100011" => -- store
                imm(11 downto 0) <= instr(31 downto 25) & instr(11 downto 7);
                imm(31 downto 12) <= (others => instr(31));
            when "0010011" => -- i-type
                if (instr(13) or (not instr(12))) = '1' then -- andi, ori, xori, 
                    imm(11 downto 0) <= instr(31 downto 20);
                    imm(31 downto 12) <= (others => instr(31));
                else                               -- slli e srli
                    imm(4 downto 0) <= instr(24 downto 20);
                    imm(31 downto 5) <= (others => instr(31));
                end if;
            when others => -- outros
                imm <= (others => 'X');
        end case;
    end process decode_instr;
end architecture;

// VHDL entity ctrl_unit, as the project stores it:
library ieee;
use ieee.std_logic_1164.all;


entity ctrl_unit is
    port(
        instr : in std_logic_vector(31 downto 0);
        pc_reg : out std_logic; -- 0 -> pc, 1 -> reg1
        alu_op : out std_logic_vector(2 downto 0); -- alu opcode
        branch : out std_logic; -- 0 -> não é branch e 1 -> é branch
        mem_read : out std_logic; -- 0 -> sem leitura, 1 -> leitura
        mem_write : out std_logic; -- 0 -> sem escrita, 1 -> escrita
        mem_to_reg : out std_logic; -- 0 -> alu, 1 -> mem
        alu_src : out std_logic; -- 0 -> reg, 1 -> imediato
        reg_write : out std_logic; -- 0 -> leitura , 1 -> escrita
        pc_reg_branch : out std_logic -- 0 -> pc, 1 -> reg1 (mux de entrada do somador do branch)
    );
end ctrl_unit;

architecture Behavioral of ctrl_unit is
begin
    -- alu_op           operação
    --  000     nop
    --  001     logico-aritmética (R-type)
    --  010     logico-aritmética (I-type)
    --  011     branch (equal or not equal)
    --  100     adição in1 + in2
    --  101     adição in1 + 1 (equal or not equal = 1)
    --  110     passa o imediato (in2) direto pra saída
    --  111     nop

    ctrl_decode : process(instr)
    begin
        case instr(6 downto 0) is
            when "0110011" => -- instruções tipo R
                reg_write <= '1'; -- escreve no reg
                mem_to_reg <= '0'; -- passa alu
                mem_write <= 'X';  -- não é mem
                mem_read <= 'X'; 
                branch <= '0'; -- sem branch
                alu_src <= '0'; -- reg
                alu_op <= "001"; -- (logico-aritmética)
                pc_reg <= '0'; -- passa reg
                pc_reg_branch <= '0'; -- passa pc
            when "0010011" => -- instruções tipo I
                reg_write <= '1';
                mem_to_reg <= '0'; -- passa alu
                mem_write <= 'X';  -- não é mem
                mem_read <= 'X'; 
                branch <= '0'; -- sem branch
                alu_src <= '1'; -- imediato
                alu_op <= "010"; -- (logico-aritmética)
                pc_reg <= '0'; -- passa reg
                pc_reg_branch <= '0'; -- passa pc
            when "1100011" => -- instruções de branch
                reg_write <= '0';
                mem_to_reg <= 'X'; -- não escreve em reg
                mem_write <= 'X';  -- não é mem
                mem_read <= 'X';
                branch <= '1'; -- branch
                alu_src <= '0'; -- reg
                alu_op <= "011"; -- (equal or not equal)
                pc_reg <= '0'; -- passa reg
                pc_reg_branch <= '0'; -- passa pc
            when "0010111" => -- auipc
                reg_write <= '1';
                mem_to_reg <= '0'; -- passa alu
                mem_write <= 'X';  -- não é mem
                mem_read <= 'X';
                branch <= '0'; -- sem branch
                alu_src <= '1'; -- imediato
                alu_op <= "100"; -- (add)
                pc_reg <= '1'; -- pc
                pc_reg_branch <= '0'; -- passa pc
            when "0110111" => -- lui
                reg_write <= '1';
                mem_to_reg <= '0'; -- passa alu
                mem_write <= 'X';  -- não é mem
                mem_read <= 'X';
                branch <= '0'; -- sem branch
                alu_src <= '1'; -- imediato
                alu_op <= "110"; -- (passa o imediato pra saída da ALU)
                pc_reg <= 'X'; -- essa entrada não é processada nessa alu_op
                pc_reg_branch <= '0'; -- passa pc
            when "0000011" => -- lw
                reg_write <= '1';
                mem_to_reg <= '1'; -- passa mem
                mem_write <= '0';  -- le na memória
                mem_read <= '1';
                branch <= '0'; -- sem branch
                alu_src <= '1'; -- imediato
                alu_op <= "100"; -- (add)
                pc_reg <= '0'; -- passa reg
                pc_reg_branch <= '0'; -- passa pc
            when "0100011" => -- sw
                reg_write <= '0';
                mem_to_reg <= 'X'; -- não escreve em reg
                mem_write <= '1';  -- escreve na memória
                mem_read <= '0';
                branch <= '0'; -- sem branch
                alu_src <= '1'; -- imediato
                alu_op <= "100"; -- (add)
                pc_reg <= '0'; -- passa reg
                pc_reg_branch <= '0'; -- passa pc
            when "1101111" => -- jal
                reg_write <= '1';
                mem_to_reg <= '0'; -- passa alu
                mem_write <= 'X';  -- não é mem
                mem_read <= 'X';
                branch <= '1'; -- branch
                alu_src <= 'X'; -- tanto faz o que entra na segunda entrada 
                alu_op <= "101"; --(add + 4)
                pc_reg <= '1'; -- passa pc
                pc_reg_branch <= '0'; -- passa pc
            when "1100111" => -- jalr
                reg_write <= '1';
                mem_to_reg <= '0'; -- passa alu
                mem_write <= 'X';  -- não é mem
                mem_read <= 'X';
                branch <= '1'; -- branch
                alu_src <= 'X'; -- tanto faz o que entra na segunda entrada
                alu_op <= "101"; --(add + 4)
                pc_reg <= '1'; -- passa pc
                pc_reg_branch <= '1'; -- passa reg1
            when others =>
                reg_write <= 'X';
                mem_to_reg <= 'X';
                mem_write <= 'X'; 
                mem_read <= 'X';
                branch <= 'X'; 
                alu_src <= 'X'; 
                alu_op <= "XXX";
                pc_reg <= 'X'; 
                pc_reg_branch <= 'X';
        end case;
    end process ctrl_decode;
end architecture;

// VHDL entity alu, as the project stores it:
library ieee;
use ieee.std_logic_1164.all;
use ieee.numeric_std.all;

entity alu is
    port(
        in_a, in_b : in std_logic_vector(31 downto 0);
        op : in std_logic_vector(3 downto 0);
        out_r : out std_logic_vector(31 downto 0);
        aux_br : out std_logic
    );
end alu;

-- Operação  OPCODE  Br_aux
-- nop        0000     0
-- Soma       0001     0 
-- Sub        0010     0
-- and        0011     0
-- or         0100     0
-- xor        0101     0
-- sll        0110     0
-- srl        0111     0
-- equal      1000     1 if equal
-- ~equal     1001     1 if not equal
-- in1 + 1    1010     1
-- out = in2  1011     0
-- nop        others   0
architecture Behavioral of alu is
    begin

    process(in_a, in_b, op)
    begin
        case op is
            when "0001" => 
                out_r <= std_logic_vector(signed(in_a) + signed(in_b));
                aux_br <= '0';
            when "0010" => 
                out_r <= std_logic_vector(signed(in_a) - signed(in_b));
                aux_br <= '0';
            when "0011" => 
                out_r <= in_a and in_b;
                aux_br <= '0';
            when "0100" =>
                out_r <= in_a or in_b;
            when "0101" => 
                out_r <= in_a xor in_b;
                aux_br <= '0';
            when "0110" => 
                out_r <= std_logic_vector(shift_left(unsigned(in_a), to_integer(unsigned(in_b(4 downto 0)))));
                aux_br <= '0';
            when "0111" => 
                out_r <= std_logic_vector(shift_right(unsigned(in_a), to_integer(unsigned(in_b(4 downto 0)))));
                aux_br <= '0';
            when "1000" => 
                out_r <= (others => '0');
                if in_a = in_b then
                	aux_br <= '1';
                else aux_br <= '0';
                end if;
            when "1001" => 
                out_r <= (others => '0');
                if in_a /= in_b then
                	aux_br <= '1';
                else aux_br <= '0';
                end if;
            when "1010" => 
                out_r <= std_logic_vector(unsigned(in_a) + 1);
                aux_br <= '1';
            when "1011" => 
                out_r <= in_b;
                aux_br <= '0';
            when others => 
                out_r <= in_a;
                aux_br <= '0';
        end case;
    end process;
end Behavioral;

// VHDL entity alu_ctrl, as the project stores it:
library ieee;
use ieee.std_logic_1164.all;

entity alu_ctrl is
    port(
        alu_op: in std_logic_vector(2 downto 0);
        instruction: in std_logic_vector(31 downto 0);
        opcode: out std_logic_vector(3 downto 0)
    );
end alu_ctrl;

-- Operação  OPCODE  Br_aux
-- nop        0000     0
-- Soma       0001     0 
-- Sub        0010     0
-- and        0011     0
-- or         0100     0
-- xor        0101     0
-- sll        0110     0
-- srl        0111     0
-- equal      1000     1 if equal
-- ~equal     1001     1 if not equal
-- in1 + 1    1010     1
-- out = in2  1011     0
-- nop        others   0

architecture Behavioral of alu_ctrl is
    signal funct3 : std_logic_vector(2 downto 0) := (others => '0');
    signal funct7 : std_logic_vector(6 downto 0) := (others => '0');

begin

    funct3 <= instruction(14 downto 12);
    funct7 <= instruction(31 downto 25);

    op_decode: process(alu_op, funct3, funct7) is
        begin
        	  opcode <= "0000";
            if alu_op = "001" or alu_op = "010" then
                if funct3 = "000" and alu_op = "001" then
	                if funct7 = "0000000" then -- add
	                    opcode <= "0001";
	                elsif funct7 = "0100000" then -- sub
	                    opcode <= "0010";
	                end if;
	           elsif funct3 = "000" and alu_op = "010" then
	           	opcode <= "0001";
	           elsif funct3 = "001" then -- sll
	                opcode <= "0110";
	           elsif funct3 = "100" then -- xor
	                opcode <= "0101";
	           elsif funct3 = "101" then -- srl
	                opcode <= "0111";
	           elsif funct3 = "110" then -- or
	                opcode <= "0100";
	           elsif funct3 = "111" then -- and
	                opcode <= "0011";
	           end if;
            elsif alu_op = "011" then
                if funct3 = "000" then -- beq
                    opcode <= "1000";
                elsif funct3 = "001" then -- bne
                    opcode <= "1001";
                end if;
            elsif alu_op = "100" then
                opcode <= "0001";
            elsif alu_op = "101" then
                opcode <= "1010";
            elsif alu_op = "110" then
                opcode <= "1011";
            elsif alu_op = "111" or alu_op = "000" then
                opcode <= "0000";
            end if;
    end process op_decode;

end Behavioral;

// VHDL entity IF_ID, as the project stores it:
library ieee;
use ieee.std_logic_1164.all;

entity IF_ID is
    port(
        clk : in std_logic;
        instr_in: in std_logic_vector(31 downto 0);
        pc_in : in std_logic_vector(31 downto 0);

        instr_out: out std_logic_vector(31 downto 0);
        pc_out : out std_logic_vector(31 downto 0)
    );
end IF_ID;

architecture Behavioral of IF_ID is
    begin
        process(clk)
        begin
            if rising_edge(clk) then
                instr_out <= instr_in;
                pc_out <= pc_in;
            end if;
        end process;
end Behavioral;

// VHDL entity ID_EX, as the project stores it:
library ieee;
use ieee.std_logic_1164.all;

entity ID_EX is
    port(
        clk : in std_logic;
        -- data
        instr_in: in std_logic_vector(31 downto 0);
        pc_in : in std_logic_vector(31 downto 0);

        instr_out: out std_logic_vector(31 downto 0);
        pc_out : out std_logic_vector(31 downto 0);

        reg_a_out : out std_logic_vector(31 downto 0);
        reg_b_out : out std_logic_vector(31 downto 0);
        reg_a_in : in std_logic_vector(31 downto 0);
        reg_b_in : in std_logic_vector(31 downto 0);

        imm_in : in std_logic_vector(31 downto 0);
        imm_out : out std_logic_vector(31 downto 0);

        -- control
        -- EX
        pc_reg_alu_in : in std_logic;
        pc_reg_alu_out : out std_logic;
        alu_src_in : in std_logic;
        alu_src_out : out std_logic;
        alu_op_in : in std_logic_vector(2 downto 0);
        alu_op_out : out std_logic_vector(2 downto 0);

        -- MEM
        mem_w_in : in std_logic;
        mem_w_out : out std_logic;
        mem_r_in : in std_logic;
        mem_r_out : out std_logic;
        branch_in : in std_logic;
        branch_out : out std_logic;
        pc_reg_br_in : in std_logic;
        pc_reg_br_out : out std_logic;

        -- WB
        mem_to_reg_in : in std_logic;
        mem_to_reg_out : out std_logic;
        reg_w_in : in std_logic;
        reg_w_out : out std_logic
    );
end ID_EX;

architecture Behavioral of ID_EX is
    begin
        process(clk)
        begin
            if rising_edge(clk) then
                instr_out <= instr_in;
                pc_out <= pc_in;

                reg_a_out <= reg_a_in;
                reg_b_out <= reg_b_in;
                imm_out <= imm_in;

                pc_reg_alu_out <= pc_reg_alu_in;
                alu_src_out <= alu_src_in;
                alu_op_out <= alu_op_in;
                mem_w_out <= mem_w_in;
                mem_r_out <= mem_r_in;
                branch_out <= branch_in;
                pc_reg_br_out <= pc_reg_br_in;
                mem_to_reg_out <= mem_to_reg_in;
                reg_w_out <= reg_w_in;
            end if;
        end process;
end Behavioral;

// VHDL entity EX_MEM, as the project stores it:
library ieee;
use ieee.std_logic_1164.all;

entity EX_MEM is
    port(
        clk : in std_logic;
        
        alu_result_in : in std_logic_vector(31 downto 0);
        branch_alu_in : in std_logic;
        reg_a_in : in std_logic_vector(31 downto 0);
        reg_b_in : in std_logic_vector(31 downto 0);
        imm_in : in std_logic_vector(31 downto 0);
        wb_addr_in : in std_logic_vector(4 downto 0);
        pc_in : in std_logic_vector(31 downto 0);

        imm_out : out std_logic_vector(31 downto 0);
        reg_a_out : out std_logic_vector(31 downto 0);
        reg_b_out : out std_logic_vector(31 downto 0);
        alu_result_out : out std_logic_vector(31 downto 0);
        branch_alu_out : out std_logic;
        wb_addr_out : out std_logic_vector(4 downto 0);
        pc_out : out std_logic_vector(31 downto 0);

        -- control
        -- MEM
        mem_w_in : in std_logic;
        mem_w_out : out std_logic;
        mem_r_in : in std_logic;
        mem_r_out : out std_logic;
        branch_in : in std_logic;
        branch_out : out std_logic;
        pc_reg_br_in : in std_logic;
        pc_reg_br_out : out std_logic;

        -- WB
        mem_to_reg_in : in std_logic;
        mem_to_reg_out : out std_logic;
        reg_w_in : in std_logic;
        reg_w_out : out std_logic
    );
end EX_MEM;

architecture Behavioral of EX_MEM is
    begin
        process(clk)
        begin
            if rising_edge(clk) then
                imm_out <= imm_in;
                reg_a_out <= reg_a_in;
                reg_b_out <= reg_b_in;
                alu_result_out <= alu_result_in;
                branch_alu_out <= branch_alu_in;
                wb_addr_out <= wb_addr_in;
                pc_out <= pc_in;

                mem_w_out <= mem_w_in;
                mem_r_out <= mem_r_in;
                branch_out <= branch_in;
                pc_reg_br_out <= pc_reg_br_in;
                mem_to_reg_out <= mem_to_reg_in;
                reg_w_out <= reg_w_in;
            end if;
        end process;
end Behavioral;

// VHDL entity MEM_WB, as the project stores it:
library ieee;
use ieee.std_logic_1164.all;

entity MEM_WB is
    port(
        clk : in std_logic;
        
        alu_result_in : in std_logic_vector(31 downto 0);
        mem_in : in std_logic_vector(31 downto 0);
        wb_addr_in : in std_logic_vector(4 downto 0);

        alu_result_out : out std_logic_vector(31 downto 0);
        mem_out : out std_logic_vector(31 downto 0);

        wb_addr_out : out std_logic_vector(4 downto 0);

        -- control
        -- WB
        mem_to_reg_in : in std_logic;
        mem_to_reg_out : out std_logic;
        reg_w_in : in std_logic;
        reg_w_out : out std_logic
    );
end MEM_WB;

architecture Behavioral of MEM_WB is
    begin
        process(clk)
        begin
            if rising_edge(clk) then
                alu_result_out <= alu_result_in;
                mem_out <= mem_in;
                wb_addr_out <= wb_addr_in;

                mem_to_reg_out <= mem_to_reg_in;
                reg_w_out <= reg_w_in;
            end if;
        end process;
end Behavioral;

// VHDL entity fwd_unit, as the project stores it:
library ieee;
use ieee.std_logic_1164.all;
use ieee.numeric_std.all;

entity fwd_unit is
    port(
        reg_s1 : in std_logic_vector(4 downto 0);
        reg_s2 : in std_logic_vector(4 downto 0);
        reg_dst : in std_logic_vector(4 downto 0);

        mem_wb_reg_dst : in std_logic_vector(4 downto 0);
        ex_mem_reg_dst : in std_logic_vector(4 downto 0);

        -- flags control ex/mem e mem/wb
        ex_mem_reg_w : in std_logic;
        mem_wb_reg_w : in std_logic;

        forward_a : out std_logic_vector(1 downto 0);
        forward_b : out std_logic_vector(1 downto 0);
        forward_c : out std_logic
    );
end fwd_unit;

architecture Behavioral of fwd_unit is
    begin
        forward_decode : process(reg_s1, reg_s2, reg_dst, mem_wb_reg_dst, ex_mem_reg_dst, ex_mem_reg_w, mem_wb_reg_w) is
            begin
            	 forward_a <= "00";
            	 forward_b <= "00";
            	 forward_c <= '0';
            	
                if (ex_mem_reg_w = '1') and (ex_mem_reg_dst /= "00000") then
                    if (ex_mem_reg_dst = reg_s1) then
                        forward_a <= "10";
                    end if;
                    if (ex_mem_reg_dst = reg_s2) then
                        forward_b <= "10";
                        forward_c <= '1';
                    end if;
                end if;
			 
                if (mem_wb_reg_w = '1') and (mem_wb_reg_dst /= "00000") and not (ex_mem_reg_w ='1' and (ex_mem_reg_dst /= "00000") and (ex_mem_reg_dst = reg_s1)) and (mem_wb_reg_dst = reg_s1) then
                    forward_a <= "01";
                end if;
                if (mem_wb_reg_w = '1') and (mem_wb_reg_dst /= "00000") and not (ex_mem_reg_w ='1' and (ex_mem_reg_dst /= "00000") and (ex_mem_reg_dst = reg_s2)) and (mem_wb_reg_dst = reg_s2) then
                    forward_b <= "01";
                end if;

        end process forward_decode;
end Behavioral;
