// Logisim project circuito_cpu_com_SIMD.circ as structural Verilog
module main (
);

  wire alu_block_aux_br, alu_br, alu_src, br, branch_en_out, bubble, clk, EX_MEM_reg_mem_r_out,
       EX_MEM_reg_mem_to_reg_out, EX_MEM_reg_mem_w_out, EX_MEM_reg_reg_w_out, flush, fwd_c, ID_EX_br_in,
       ID_EX_pc_reg_br, ID_EX_reg_alu_src_out, ID_EX_reg_branch_out, ID_EX_reg_mem_r_out,
       ID_EX_reg_mem_to_reg_out, ID_EX_reg_mem_w_out, ID_EX_reg_pc_reg_alu_out, ID_EX_reg_pc_reg_br_out,
       ID_EX_reg_reg_w_out, if_id_w, mem_r, mem_reg, mem_w, MEM_WB_reg_mem_to_reg_out, MEM_WB_reg_reg_w_out,
       pc_reg_alu, pc_reg_br, pc_write, subctrlsys_reg_write, vetorial_op;
  wire [1:0] fwd_a, fwd_b;
  wire [2:0] alu_op, ID_EX_reg_alu_op_out;
  wire [3:0] alu_ctrl_sys_opcode;
  wire [4:0] EX_MEM_reg_wb_addr_out, ID_EX_reg_instr_out_2, ID_EX_reg_instr_out_3, MEM_WB_reg_wb_addr_out,
       reg_dst;
  wire [31:0] alu_block_out_r, EX_MEM_alu_result, EX_MEM_reg_imm_out, EX_MEM_reg_pc_out,
       EX_MEM_reg_reg_a_out, EX_MEM_reg_reg_b_out, ID_EX_imm, ID_EX_pc, ID_EX_reg_a, ID_EX_reg_b,
       ID_EX_reg_instr_out, IF_ID_pc, IF_ID_reg_instr_out, immediate_gen_imm, MEM_WB_reg_alu_result_out,
       MEM_WB_reg_mem_out, MEM_WB_result, multiplexer_1_out, multiplexer_2_out, multiplexer_3_out,
       multiplexer_4_out, multiplexer_5_out, program_counter_pc, program_mem_data, reg_b_ex_mem_in,
       register_file_reg_a_data, register_file_reg_b_data, SIMD_ALU_s_o;

  and branch_en (branch_en_out, alu_br, br);
  prog_count program_counter (
    .clk(clk), .imm(EX_MEM_reg_imm_out), .branch(branch_en_out), .pc_reg_mux(pc_reg_br),
    .reg_in(EX_MEM_reg_reg_a_out), .pc_in(EX_MEM_reg_pc_out), .pc_w(pc_write), .pc(program_counter_pc));
  ROM #(.addrWidth(24), .dataWidth(32)) program_mem (.addr(program_counter_pc[23:0]), .data(program_mem_data));
  IF_ID IF_ID_reg (
    .clk(clk), .instr_in(program_mem_data), .pc_in(program_counter_pc), .write(if_id_w), .flush(flush),
    .instr_out(IF_ID_reg_instr_out), .pc_out(IF_ID_pc));
  hzd_unit hazard_unit (
    .id_ex_mem_r(ID_EX_reg_mem_w_out), .id_ex_reg_dst(reg_dst), .if_id_reg_s1(IF_ID_reg_instr_out[19:15]),
    .if_id_reg_s2(IF_ID_reg_instr_out[24:20]), .pc_write(pc_write), .if_id_write(if_id_w), .bubble(bubble));
  ctrl_unit subctrlsys (
    .instr(IF_ID_reg_instr_out), .pc_reg(pc_reg_alu), .alu_op(alu_op), .branch(ID_EX_br_in),
    .mem_read(mem_r), .mem_write(mem_w), .mem_to_reg(mem_reg), .alu_src(alu_src),
    .reg_write(subctrlsys_reg_write), .pc_reg_branch(ID_EX_pc_reg_br));
  reg_file register_file (
    .clk(clk), .write_en(MEM_WB_reg_reg_w_out), .write_data(MEM_WB_result),
    .write_addr(MEM_WB_reg_wb_addr_out), .reg_a_addr(IF_ID_reg_instr_out[19:15]),
    .reg_b_addr(IF_ID_reg_instr_out[24:20]), .reg_a_data(register_file_reg_a_data),
    .reg_b_data(register_file_reg_b_data));
  imm_gen immediate_gen (.instr(IF_ID_reg_instr_out), .imm(immediate_gen_imm));
  ID_EX ID_EX_reg (
    .clk(clk), .instr_in(IF_ID_reg_instr_out), .pc_in(IF_ID_pc), .reg_a_in(register_file_reg_a_data),
    .reg_b_in(register_file_reg_b_data), .imm_in(immediate_gen_imm), .pc_reg_alu_in(pc_reg_alu),
    .alu_src_in(alu_src), .alu_op_in(alu_op), .mem_w_in(mem_w), .mem_r_in(mem_r), .branch_in(ID_EX_br_in),
    .pc_reg_br_in(ID_EX_pc_reg_br), .mem_to_reg_in(mem_reg), .reg_w_in(subctrlsys_reg_write), .flush(flush),
    .bubble(bubble),
    .instr_out({ID_EX_reg_instr_out[31:25], ID_EX_reg_instr_out_3, ID_EX_reg_instr_out_2, ID_EX_reg_instr_out[14:12], reg_dst, ID_EX_reg_instr_out[6:0]}),
    .pc_out(ID_EX_pc), .reg_a_out(ID_EX_reg_a), .reg_b_out(ID_EX_reg_b), .imm_out(ID_EX_imm),
    .pc_reg_alu_out(ID_EX_reg_pc_reg_alu_out), .alu_src_out(ID_EX_reg_alu_src_out),
    .alu_op_out(ID_EX_reg_alu_op_out), .mem_w_out(ID_EX_reg_mem_w_out), .mem_r_out(ID_EX_reg_mem_r_out),
    .branch_out(ID_EX_reg_branch_out), .pc_reg_br_out(ID_EX_reg_pc_reg_br_out),
    .mem_to_reg_out(ID_EX_reg_mem_to_reg_out), .reg_w_out(ID_EX_reg_reg_w_out));
  Multiplexer #(.enable("false"), .select(2), .width(32)) multiplexer_1 (
    .in0(ID_EX_reg_a), .in1(MEM_WB_result), .in2(EX_MEM_alu_result), .in3({32{1'b0}}),
    .out(multiplexer_1_out), .sel(fwd_a));
  Clock clk_logisim (.out(clk));
  Multiplexer #(.enable("false"), .select(2), .width(32)) multiplexer_2 (
    .in0(ID_EX_reg_b), .in1(MEM_WB_result), .in2(EX_MEM_alu_result), .in3({32{1'b0}}),
    .out(multiplexer_2_out), .sel(fwd_b));
  alu_ctrl alu_ctrl_sys (
    .alu_op(ID_EX_reg_alu_op_out),
    .instruction({ID_EX_reg_instr_out[31:25], ID_EX_reg_instr_out_3, ID_EX_reg_instr_out_2, ID_EX_reg_instr_out[14:12], reg_dst, ID_EX_reg_instr_out[6:0]}),
    .opcode(alu_ctrl_sys_opcode), .vetorial(vetorial_op));
  Multiplexer #(.enable("false"), .width(32)) multiplexer_3 (
    .in0(multiplexer_1_out), .in1(ID_EX_pc), .out(multiplexer_3_out), .sel(ID_EX_reg_pc_reg_alu_out));
  Multiplexer #(.enable("false"), .width(32)) multiplexer_4 (
    .in0(multiplexer_2_out), .in1(ID_EX_imm), .out(multiplexer_4_out), .sel(ID_EX_reg_alu_src_out));
  alu_simd SIMD_ALU (
    .A_i(multiplexer_3_out), .B_i(multiplexer_4_out),
    .instruction({ID_EX_reg_instr_out[31:25], ID_EX_reg_instr_out_3, ID_EX_reg_instr_out_2, ID_EX_reg_instr_out[14:12], reg_dst, ID_EX_reg_instr_out[6:0]}),
    .opcode(alu_ctrl_sys_opcode), .S_o(SIMD_ALU_s_o));
  alu alu_block (
    .in_a(multiplexer_3_out), .in_b(multiplexer_4_out), .op(alu_ctrl_sys_opcode), .out_r(alu_block_out_r),
    .aux_br(alu_block_aux_br));
  Multiplexer #(.enable("false"), .width(32)) multiplexer_5 (
    .in0(alu_block_out_r), .in1(SIMD_ALU_s_o), .out(multiplexer_5_out), .sel(vetorial_op));
  fwd_unit forwarding_unit (
    .reg_s1(ID_EX_reg_instr_out_2), .reg_s2(ID_EX_reg_instr_out_3), .reg_dst(reg_dst),
    .mem_wb_reg_dst(MEM_WB_reg_wb_addr_out), .ex_mem_reg_dst(EX_MEM_reg_wb_addr_out),
    .ex_mem_reg_w(EX_MEM_reg_reg_w_out), .mem_wb_reg_w(MEM_WB_reg_reg_w_out), .forward_a(fwd_a),
    .forward_b(fwd_b), .forward_c(fwd_c));
  Multiplexer #(.enable("false"), .width(32)) multiplexer_6 (
    .in0(ID_EX_reg_b), .in1(EX_MEM_alu_result), .out(reg_b_ex_mem_in), .sel(fwd_c));
  EX_MEM EX_MEM_reg (
    .clk(clk), .alu_result_in(multiplexer_5_out), .branch_alu_in(alu_block_aux_br), .reg_a_in(ID_EX_reg_a),
    .reg_b_in(reg_b_ex_mem_in), .imm_in(ID_EX_imm), .wb_addr_in(reg_dst), .pc_in(ID_EX_pc),
    .mem_w_in(ID_EX_reg_mem_w_out), .mem_r_in(ID_EX_reg_mem_r_out), .branch_in(ID_EX_reg_branch_out),
    .pc_reg_br_in(ID_EX_reg_pc_reg_br_out), .mem_to_reg_in(ID_EX_reg_mem_to_reg_out),
    .reg_w_in(ID_EX_reg_reg_w_out), .imm_out(EX_MEM_reg_imm_out), .reg_a_out(EX_MEM_reg_reg_a_out),
    .reg_b_out(EX_MEM_reg_reg_b_out), .alu_result_out(EX_MEM_alu_result), .branch_alu_out(alu_br),
    .wb_addr_out(EX_MEM_reg_wb_addr_out), .pc_out(EX_MEM_reg_pc_out), .mem_w_out(EX_MEM_reg_mem_w_out),
    .mem_r_out(EX_MEM_reg_mem_r_out), .branch_out(br), .pc_reg_br_out(pc_reg_br),
    .mem_to_reg_out(EX_MEM_reg_mem_to_reg_out), .reg_w_out(EX_MEM_reg_reg_w_out));
  RAM #(.addrWidth(24), .dataWidth(32), .databus("bidir"), .enables("line"), .trigger("falling")) data_mem (
    .addr(EX_MEM_alu_result[23:0]), .we(EX_MEM_reg_mem_w_out), .oe(EX_MEM_reg_mem_r_out), .clk(clk),
    .data(EX_MEM_reg_reg_b_out));
  mem_br_taken br_flusher (.alu_br(alu_br), .branch(br), .flush(flush));
  MEM_WB MEM_WB_reg (
    .clk(clk), .alu_result_in(EX_MEM_alu_result), .mem_in(EX_MEM_reg_reg_b_out),
    .wb_addr_in(EX_MEM_reg_wb_addr_out), .mem_to_reg_in(EX_MEM_reg_mem_to_reg_out),
    .reg_w_in(EX_MEM_reg_reg_w_out), .alu_result_out(MEM_WB_reg_alu_result_out),
    .mem_out(MEM_WB_reg_mem_out), .wb_addr_out(MEM_WB_reg_wb_addr_out),
    .mem_to_reg_out(MEM_WB_reg_mem_to_reg_out), .reg_w_out(MEM_WB_reg_reg_w_out));
  Multiplexer #(.enable("false"), .width(32)) multiplexer_7 (
    .in0(MEM_WB_reg_alu_result_out), .in1(MEM_WB_reg_mem_out), .out(MEM_WB_result),
    .sel(MEM_WB_reg_mem_to_reg_out));

  // Notes on the sheet:
  //   contents of program_mem (hex, n*v repeats v):
  //   7ff00313 7ff30313 130313 c00613 c313b3 6383b3 333 7002b3 532023 130313 fe731ee3 63
endmodule

// VHDL entity prog_count, as the project stores it:
library ieee;
use ieee.std_logic_1164.all;
use ieee.numeric_std.all;

entity prog_count is
    port(
        clk : in std_logic;
        imm : in std_logic_vector(31 downto 0);
        branch : in std_logic;
        pc_reg_mux : in std_logic;
        reg_in : in std_logic_vector(31 downto 0);
        pc_in : in std_logic_vector(31 downto 0);
        pc : out std_logic_vector(31 downto 0);
        pc_w : in std_logic
    );
end prog_count;

architecture Behavioral of prog_count is
    signal immediate, ptr_pc : std_logic_vector(31 downto 0) := (others => '0');
    begin
        immediate <= imm;
        pc <= ptr_pc;

        fetch_instr: process(clk, branch, pc_reg_mux, pc_in, reg_in, pc_w) is
        begin
            if rising_edge(clk) and pc_w = '1' then
                if branch = '1' then
                	if pc_reg_mux = '0' then
                    	ptr_pc <= std_logic_vector(signed(pc_in) + signed(immediate));
                    else
                    	ptr_pc <= std_logic_vector(signed(reg_in) + signed(immediate));
                    end if;
                else
                    ptr_pc <= std_logic_vector(unsigned(ptr_pc) + x"00000001");
                end if;
            end if;
        end process fetch_instr;
end Behavioral;

// VHDL entity reg_file, as the project stores it:
library ieee;
use ieee.std_logic_1164.all;
use ieee.numeric_std.all;

entity reg_file is
    port(
        clk : in std_logic;
        write_en : in std_logic;

        write_data : in std_logic_vector(31 downto 0);
        
        write_addr : in std_logic_vector(4 downto 0);
        reg_a_addr : in std_logic_vector(4 downto 0);
        reg_b_addr : in std_logic_vector(4 downto 0);

        reg_a_data : out std_logic_vector(31 downto 0);
        reg_b_data : out std_logic_vector(31 downto 0)
    );
end reg_file;

architecture Behavioral of reg_file is
    -- 32 registradores de 32 bits
    type register_mem is array (integer range <>) of std_logic_vector(31 downto 0);
    signal register_bank : register_mem(0 to 31) := (others => x"00000000");

    begin      
    	   reg_a_data <= register_bank(to_integer(unsigned(reg_a_addr)));
        reg_b_data <= register_bank(to_integer(unsigned(reg_b_addr)));
        register_access: process(clk, write_en, write_addr) is
        begin
            -- na borda de descida
            if falling_edge(clk) and write_en = '1' then
            	if write_addr /= "00000" then
            		register_bank(to_integer(unsigned(write_addr))) <= write_data;
            	end if;
            end if;
        end process register_access;

end Behavioral;

// VHDL entity imm_gen, as the project stores it:
library ieee;
use ieee.std_logic_1164.all;
use ieee.numeric_std.all;

entity imm_gen is
    port(
        instr : in std_logic_vector(31 downto 0);
        imm : out std_logic_vector(31 downto 0)
    );
end imm_gen;

architecture Behavioral of imm_gen is
begin
    decode_instr : process(instr)
    begin
        -- logica para fazer decode da instrução
        case instr(6 downto 0) is
            when "0110111" => -- lui
                imm(31 downto 12) <= instr(31 downto 12);
                imm(11 downto 0) <= (others => '0');
            when "0010111" => -- auipc
                imm(31 downto 12) <= instr(31 downto 12);
                imm(11 downto 0) <= (others => '0');
            when "1101111" => -- jal
                imm(19 downto 0) <= instr(31) & instr(19 downto 12) & instr(20) & instr(30 downto 21);
                imm(31 downto 20) <= (others => instr(31));
            when "1100111" => -- jalr
                imm(11 downto 0) <= instr(31 downto 20);
                imm(31 downto 12) <= (others => instr(31));
            when "1100011" => -- branch
                imm(11 downto 0) <= instr(31) & instr(7) & instr(30 downto 25) & instr(11 downto 8);
                imm(31 downto 12) <= (others => instr(31));
            when "0000011" => -- load
                imm(11 downto 0) <= instr(31 downto 20);
                imm(31 downto 12) <= (others => instr(31));
            when "0100011" => -- store
                imm(11 downto 0) <= instr(31 downto 25) & instr(11 downto 7);
                imm(31 downto 12) <= (others => instr(31));
            when "0010011" => -- i-type
                if (instr(13) or (not instr(12))) = '1' then -- andi, ori, xori, 
                    imm(11 downto 0) <= instr(31 downto 20);
                    imm(31 downto 12) <= (others => instr(31));
                else                               -- slli e srli
                    imm(4 downto 0) <= instr(24 downto 20);
                    imm(31 downto 5) <= (others => instr(31));
                end if;
            when others => -- outros
                imm <= (others => 'X');
        end case;
    end process decode_instr;
end architecture;

// VHDL entity ctrl_unit, as the project stores it:
library ieee;
use ieee.std_logic_1164.all;


entity ctrl_unit is
    port(
        instr : in std_logic_vector(31 downto 0);
        pc_reg : out std_logic; -- 0 -> pc, 1 -> reg1
        alu_op : out std_logic_vector(2 downto 0); -- alu opcode
        branch : out std_logic; -- 0 -> não é branch e 1 -> é branch
        mem_read : out std_logic; -- 0 -> sem leitura, 1 -> leitura
        mem_write : out std_logic; -- 0 -> sem escrita, 1 -> escrita
        mem_to_reg : out std_logic; -- 0 -> alu, 1 -> mem
        alu_src : out std_logic; -- 0 -> reg, 1 -> imediato
        reg_write : out std_logic; -- 0 -> leitura , 1 -> escrita
        pc_reg_branch : out std_logic -- 0 -> pc, 1 -> reg1 (mux de entrada do somador do branch)
    );
end ctrl_unit;

architecture Behavioral of ctrl_unit is
begin
    -- alu_op           operação
    --  000     nop
    --  001     logico-aritmética (R-type)
    --  010     logico-aritmética (I-type)
    --  011     branch (equal or not equal)
    --  100     adição in1 + in2
    --  101     adição in1 + 1 (equal or not equal = 1)
    --  110     passa o imediato (in2) direto pra saída
    --  111     nop

    ctrl_decode : process(instr)
    begin
        case instr(6 downto 0) is
            when "0110011" => -- instruções tipo R
                reg_write <= '1'; -- escreve no reg
                mem_to_reg <= '0'; -- passa alu
                mem_write <= 'X';  -- não é mem
                mem_read <= 'X'; 
                branch <= '0'; -- sem branch
                alu_src <= '0'; -- reg
                alu_op <= "001"; -- (logico-aritmética)
                pc_reg <= '0'; -- passa reg
                pc_reg_branch <= '0'; -- passa pc
            when "0010011" => -- instruções tipo I
                reg_write <= '1';
                mem_to_reg <= '0'; -- passa alu
                mem_write <= 'X';  -- não é mem
                mem_read <= 'X'; 
                branch <= '0'; -- sem branch
                alu_src <= '1'; -- imediato
                alu_op <= "010"; -- (logico-aritmética)
                pc_reg <= '0'; -- passa reg
                pc_reg_branch <= '0'; -- passa pc
            when "1100011" => -- instruções de branch
                reg_write <= '0';
                mem_to_reg <= 'X'; -- não escreve em reg
                mem_write <= 'X';  -- não é mem
                mem_read <= 'X';
                branch <= '1'; -- branch
                alu_src <= '0'; -- reg
                alu_op <= "011"; -- (equal or not equal)
                pc_reg <= '0'; -- passa reg
                pc_reg_branch <= '0'; -- passa pc
            when "0010111" => -- auipc
                reg_write <= '1';
                mem_to_reg <= '0'; -- passa alu
                mem_write <= 'X';  -- não é mem
                mem_read <= 'X';
                branch <= '0'; -- sem branch
                alu_src <= '1'; -- imediato
                alu_op <= "100"; -- (add)
                pc_reg <= '1'; -- pc
                pc_reg_branch <= '0'; -- passa pc
            when "0110111" => -- lui
                reg_write <= '1';
                mem_to_reg <= '0'; -- passa alu
                mem_write <= 'X';  -- não é mem
                mem_read <= 'X';
                branch <= '0'; -- sem branch
                alu_src <= '1'; -- imediato
                alu_op <= "110"; -- (passa o imediato pra saída da ALU)
                pc_reg <= 'X'; -- essa entrada não é processada nessa alu_op
                pc_reg_branch <= '0'; -- passa pc
            when "0000011" => -- lw
                reg_write <= '1';
                mem_to_reg <= '1'; -- passa mem
                mem_write <= '0';  -- le na memória
                mem_read <= '1';
                branch <= '0'; -- sem branch
                alu_src <= '1'; -- imediato
                alu_op <= "100"; -- (add)
                pc_reg <= '0'; -- passa reg
                pc_reg_branch <= '0'; -- passa pc
            when "0100011" => -- sw
                reg_write <= '0';
                mem_to_reg <= 'X'; -- não escreve em reg
                mem_write <= '1';  -- escreve na memória
                mem_read <= '0';
                branch <= '0'; -- sem branch
                alu_src <= '1'; -- imediato
                alu_op <= "100"; -- (add)
                pc_reg <= '0'; -- passa reg
                pc_reg_branch <= '0'; -- passa pc
            when "1101111" => -- jal
                reg_write <= '1';
                mem_to_reg <= '0'; -- passa alu
                mem_write <= 'X';  -- não é mem
                mem_read <= 'X';
                branch <= '1'; -- branch
                alu_src <= 'X'; -- tanto faz o que entra na segunda entrada 
                alu_op <= "101"; --(add + 4)
                pc_reg <= '1'; -- passa pc
                pc_reg_branch <= '0'; -- passa pc
            when "1100111" => -- jalr
                reg_write <= '1';
                mem_to_reg <= '0'; -- passa alu
                mem_write <= 'X';  -- não é mem
                mem_read <= 'X';
                branch <= '1'; -- branch
                alu_src <= 'X'; -- tanto faz o que entra na segunda entrada
                alu_op <= "101"; --(add + 4)
                pc_reg <= '1'; -- passa pc
                pc_reg_branch <= '1'; -- passa reg1
            when "0001111" => -- SIMD tipo R
                reg_write <= '1'; -- escreve no reg
                mem_to_reg <= '0'; -- passa alu
                mem_write <= 'X';  -- não é mem
                mem_read <= 'X'; 
                branch <= '0'; -- sem branch
                alu_src <= '0'; -- reg
                alu_op <= "001"; -- (logico-aritmética R)
                pc_reg <= '0'; -- passa reg
                pc_reg_branch <= '0'; -- passa pc
            when "1110011" => -- SIMD addi
                reg_write <= '1';
                mem_to_reg <= '0'; -- passa alu
                mem_write <= 'X';  -- não é mem
                mem_read <= 'X'; 
                branch <= '0'; -- sem branch
                alu_src <= '1'; -- imediato
                alu_op <= "010"; -- (logico-aritmética I)
                pc_reg <= '0'; -- passa reg
                pc_reg_branch <= '0'; -- passa pc
            when "0011011" => -- SIMD slli
                reg_write <= '1';
                mem_to_reg <= '0'; -- passa alu
                mem_write <= 'X';  -- não é mem
                mem_read <= 'X'; 
                branch <= '0'; -- sem branch
                alu_src <= '1'; -- imediato
                alu_op <= "010"; -- (logico-aritmética I)
                pc_reg <= '0'; -- passa reg
                pc_reg_branch <= '0'; -- passa pc
            when "0111011" => -- SIMD srli
                reg_write <= '1';
                mem_to_reg <= '0'; -- passa alu
                mem_write <= 'X';  -- não é mem
                mem_read <= 'X'; 
                branch <= '0'; -- sem branch
                alu_src <= '1'; -- imediato
                alu_op <= "010"; -- (logico-aritmética I)
                pc_reg <= '0'; -- passa reg
                pc_reg_branch <= '0'; -- passa pc
            when others =>
                reg_write <= 'X';
                mem_to_reg <= 'X';
                mem_write <= 'X'; 
                mem_read <= 'X';
                branch <= 'X'; 
                alu_src <= 'X'; 
                alu_op <= "XXX";
                pc_reg <= 'X'; 
                pc_reg_branch <= 'X';
        end case;
    end process ctrl_decode;
end architecture;

// VHDL entity alu, as the project stores it:
library ieee;
use ieee.std_logic_1164.all;
use ieee.numeric_std.all;

entity alu is
    port(
        in_a, in_b : in std_logic_vector(31 downto 0);
        op : in std_logic_vector(3 downto 0);
        out_r : out std_logic_vector(31 downto 0);
        aux_br : out std_logic
    );
end alu;

-- Operação  OPCODE  Br_aux
-- nop        0000     0
-- Soma       0001     0 
-- Sub        0010     0
-- and        0011     0
-- or         0100     0
-- xor        0101     0
-- sll        0110     0
-- srl        0111     0
-- equal      1000     1 if equal
-- ~equal     1001     1 if not equal
-- in1 + 1    1010     1
-- out = in2  1011     0
-- nop        others   0
architecture Behavioral of alu is
    begin

    process(in_a, in_b, op)
    begin
        case op is
            when "0001" => 
                out_r <= std_logic_vector(signed(in_a) + signed(in_b));
                aux_br <= '0';
            when "0010" => 
                out_r <= std_logic_vector(signed(in_a) - signed(in_b));
                aux_br <= '0';
            when "0011" => 
                out_r <= in_a and in_b;
                aux_br <= '0';
            when "0100" =>
                out_r <= in_a or in_b;
            when "0101" => 
                out_r <= in_a xor in_b;
                aux_br <= '0';
            when "0110" => 
                out_r <= std_logic_vector(shift_left(unsigned(in_a), to_integer(unsigned(in_b(4 downto 0)))));
                aux_br <= '0';
            when "0111" => 
                out_r <= std_logic_vector(shift_right(unsigned(in_a), to_integer(unsigned(in_b(4 downto 0)))));
                aux_br <= '0';
            when "1000" => 
                out_r <= (others => '0');
                if in_a = in_b then
                	aux_br <= '1';
                else aux_br <= '0';
                end if;
            when "1001" => 
                out_r <= (others => '0');
                if in_a /= in_b then
                	aux_br <= '1';
                else aux_br <= '0';
                end if;
            when "1010" => 
                out_r <= std_logic_vector(unsigned(in_a) + 1);
                aux_br <= '1';
            when "1011" => 
                out_r <= in_b;
                aux_br <= '0';
            when others => 
                out_r <= in_a;
                aux_br <= '0';
        end case;
    end process;
end Behavioral;

// VHDL entity alu_ctrl, as the project stores it:
library ieee;
use ieee.std_logic_1164.all;

entity alu_ctrl is
    port(
        alu_op: in std_logic_vector(2 downto 0);
        instruction: in std_logic_vector(31 downto 0);
        opcode: out std_logic_vector(3 downto 0);

        vetorial : out std_logic
    );
end alu_ctrl;

-- Operação  OPCODE  Br_aux
-- nop        0000     0
-- Soma       0001     0 
-- Sub        0010     0
-- and        0011     0
-- or         0100     0
-- xor        0101     0
-- sll        0110     0
-- srl        0111     0
-- equal      1000     1 if equal
-- ~equal     1001     1 if not equal
-- in1 + 1    1010     1
-- out = in2  1011     0
-- nop        others   0

architecture Behavioral of alu_ctrl is
    signal funct3 : std_logic_vector(2 downto 0) := (others => '0');
    signal funct7, instruc_opcode : std_logic_vector(6 downto 0) := (others => '0');

begin

    funct3 <= instruction(14 downto 12);
    funct7 <= instruction(31 downto 25);
    instruc_opcode <= instruction(6 downto 0);

    op_decode: process(alu_op, funct3, funct7, instruc_opcode) is
        begin
            -- vetorial se sll/slli vetorial, srl/srli vetorial, add/sub vetorial, addi vetorial
            if (((instruc_opcode = "0001111") and ((funct3 = "001" or funct3 = "010") or (funct3 = "011" or funct3 = "100"))) or (((instruc_opcode = "1110011" or instruc_opcode = "0011011") or instruc_opcode = "0111011"))) then
                vetorial <= '1';
            else
                vetorial <= '0';
            end if;

            if alu_op = "001" or alu_op = "010" then -- se for tipo R ou tipo I
                if (funct3 = "000" and alu_op = "001") or ((instruc_opcode = "0001111") and (funct3 = "001" or funct3 = "010")) then
                    -- se add/sub ou add/sub vetorial
	                if funct7 = "0000000" or (instruc_opcode = "0001111" and funct3 = "001") then -- add ou add vetorial
	                    opcode <= "0001";
	                elsif funct7 = "0100000" or (instruc_opcode = "0001111" and funct3 = "010") then -- sub ou sub vetorial
	                    opcode <= "0010";
	                end if;
                elsif (funct3 = "000" and alu_op = "010") or instruc_opcode = "1110011" then -- addi
                    opcode <= "0001";
                elsif funct3 = "001" or (instruc_opcode = "0001111" and funct3 = "011") or instruc_opcode = "0011011" then -- sll
                    -- se sll/slli ou sll vetorial ou slli vetoril
                    opcode <= "0110";
                elsif funct3 = "100" then -- xor
                    opcode <= "0101";
                elsif funct3 = "101" or (instruc_opcode = "0001111" and funct3 = "100") or instruc_opcode = "0111011" then -- srl
                    -- se srl/srli ou srl vetorial ou srli vetorial
                    opcode <= "0111";
                elsif funct3 = "110" then -- or
                    opcode <= "0100";
                elsif funct3 = "111" then -- and
                    opcode <= "0011";
                end if;
            elsif alu_op = "011" then
                if funct3 = "000" then -- beq
                    opcode <= "1000";
                elsif funct3 = "001" then -- bne
                    opcode <= "1001";
                end if;
            elsif alu_op = "100" then
                opcode <= "0001";
            elsif alu_op = "101" then
                opcode <= "1010";
            elsif alu_op = "110" then
                opcode <= "1011";
            elsif alu_op = "111" or alu_op = "000" then
                opcode <= "0000";
            end if;
    end process op_decode;

end Behavioral;

// VHDL entity IF_ID, as the project stores it:
library ieee;
use ieee.std_logic_1164.all;

entity IF_ID is
    port(
        clk : in std_logic;
        instr_in: in std_logic_vector(31 downto 0);
        pc_in : in std_logic_vector(31 downto 0);

        instr_out: out std_logic_vector(31 downto 0);
        pc_out : out std_logic_vector(31 downto 0);

	   write : in std_logic;
        flush : in std_logic
    );
end IF_ID;

architecture Behavioral of IF_ID is
    begin
        process(clk, flush, write)
        begin
            if rising_edge(clk) and write = '1' then
                instr_out <= instr_in;
                pc_out <= pc_in;
            end if;
            if flush = '1' then
                instr_out <= (others => '0');
                pc_out <= (others => '0');
            end if;
        end process;
end Behavioral;

// VHDL entity ID_EX, as the project stores it:
library ieee;
use ieee.std_logic_1164.all;

entity ID_EX is
    port(
        clk : in std_logic;

        -- data
        instr_in: in std_logic_vector(31 downto 0);
        pc_in : in std_logic_vector(31 downto 0);

        instr_out: out std_logic_vector(31 downto 0);
        pc_out : out std_logic_vector(31 downto 0);

        reg_a_out : out std_logic_vector(31 downto 0);
        reg_b_out : out std_logic_vector(31 downto 0);
        reg_a_in : in std_logic_vector(31 downto 0);
        reg_b_in : in std_logic_vector(31 downto 0);

        imm_in : in std_logic_vector(31 downto 0);
        imm_out : out std_logic_vector(31 downto 0);

        -- control
        -- EX
        pc_reg_alu_in : in std_logic;
        pc_reg_alu_out : out std_logic;
        alu_src_in : in std_logic;
        alu_src_out : out std_logic;
        alu_op_in : in std_logic_vector(2 downto 0);
        alu_op_out : out std_logic_vector(2 downto 0);

        -- MEM
        mem_w_in : in std_logic;
        mem_w_out : out std_logic;
        mem_r_in : in std_logic;
        mem_r_out : out std_logic;
        branch_in : in std_logic;
        branch_out : out std_logic;
        pc_reg_br_in : in std_logic;
        pc_reg_br_out : out std_logic;

        -- WB
        mem_to_reg_in : in std_logic;
        mem_to_reg_out : out std_logic;
        reg_w_in : in std_logic;
        reg_w_out : out std_logic;

        -- harzard
        flush : in std_logic;
        bubble : in std_logic
    );
end ID_EX;

architecture Behavioral of ID_EX is
    begin
        process(clk, flush, bubble)
        begin
            if rising_edge(clk) and not bubble = '1' then
                instr_out <= instr_in;
                pc_out <= pc_in;

                reg_a_out <= reg_a_in;
                reg_b_out <= reg_b_in;
                imm_out <= imm_in;

                pc_reg_alu_out <= pc_reg_alu_in;
                alu_src_out <= alu_src_in;
                alu_op_out <= alu_op_in;
                mem_w_out <= mem_w_in;
                mem_r_out <= mem_r_in;
                branch_out <= branch_in;
                pc_reg_br_out <= pc_reg_br_in;
                mem_to_reg_out <= mem_to_reg_in;
                reg_w_out <= reg_w_in;
            end if;
            if flush = '1' then
                instr_out <= (others => '0');
                pc_out <= (others => '0');

                reg_a_out <= (others => '0');
                reg_b_out <= (others => '0');
                imm_out <= (others => '0');

                pc_reg_alu_out <= '0';
                alu_src_out <= '0';
                alu_op_out <= (others => '0');
                mem_w_out <= '0';
                mem_r_out <= '0';
                branch_out <= '0';
                pc_reg_br_out <= '0';
                mem_to_reg_out <= '0';
                reg_w_out <= '0';
            end if;
        end process;
end Behavioral;

// VHDL entity EX_MEM, as the project stores it:
library ieee;
use ieee.std_logic_1164.all;

entity EX_MEM is
    port(
        clk : in std_logic;
        
        alu_result_in : in std_logic_vector(31 downto 0);
        branch_alu_in : in std_logic;
        reg_a_in : in std_logic_vector(31 downto 0);
        reg_b_in : in std_logic_vector(31 downto 0);
        imm_in : in std_logic_vector(31 downto 0);
        wb_addr_in : in std_logic_vector(4 downto 0);
        pc_in : in std_logic_vector(31 downto 0);

        imm_out : out std_logic_vector(31 downto 0);
        reg_a_out : out std_logic_vector(31 downto 0);
        reg_b_out : out std_logic_vector(31 downto 0);
        alu_result_out : out std_logic_vector(31 downto 0);
        branch_alu_out : out std_logic;
        wb_addr_out : out std_logic_vector(4 downto 0);
        pc_out : out std_logic_vector(31 downto 0);

        -- control
        -- MEM
        mem_w_in : in std_logic;
        mem_w_out : out std_logic;
        mem_r_in : in std_logic;
        mem_r_out : out std_logic;
        branch_in : in std_logic;
        branch_out : out std_logic;
        pc_reg_br_in : in std_logic;
        pc_reg_br_out : out std_logic;

        -- WB
        mem_to_reg_in : in std_logic;
        mem_to_reg_out : out std_logic;
        reg_w_in : in std_logic;
        reg_w_out : out std_logic
    );
end EX_MEM;

architecture Behavioral of EX_MEM is
    begin
        process(clk)
        begin
            if rising_edge(clk) then
                imm_out <= imm_in;
                reg_a_out <= reg_a_in;
                reg_b_out <= reg_b_in;
                alu_result_out <= alu_result_in;
                branch_alu_out <= branch_alu_in;
                wb_addr_out <= wb_addr_in;
                pc_out <= pc_in;

                mem_w_out <= mem_w_in;
                mem_r_out <= mem_r_in;
                branch_out <= branch_in;
                pc_reg_br_out <= pc_reg_br_in;
                mem_to_reg_out <= mem_to_reg_in;
                reg_w_out <= reg_w_in;
            end if;
        end process;
end Behavioral;

// VHDL entity MEM_WB, as the project stores it:
library ieee;
use ieee.std_logic_1164.all;

entity MEM_WB is
    port(
        clk : in std_logic;
        
        alu_result_in : in std_logic_vector(31 downto 0);
        mem_in : in std_logic_vector(31 downto 0);
        wb_addr_in : in std_logic_vector(4 downto 0);

        alu_result_out : out std_logic_vector(31 downto 0);
        mem_out : out std_logic_vector(31 downto 0);

        wb_addr_out : out std_logic_vector(4 downto 0);

        -- control
        -- WB
        mem_to_reg_in : in std_logic;
        mem_to_reg_out : out std_logic;
        reg_w_in : in std_logic;
        reg_w_out : out std_logic
    );
end MEM_WB;

architecture Behavioral of MEM_WB is
    begin
        process(clk)
        begin
            if rising_edge(clk) then
                alu_result_out <= alu_result_in;
                mem_out <= mem_in;
                wb_addr_out <= wb_addr_in;

                mem_to_reg_out <= mem_to_reg_in;
                reg_w_out <= reg_w_in;
            end if;
        end process;
end Behavioral;

// VHDL entity fwd_unit, as the project stores it:
library ieee;
use ieee.std_logic_1164.all;
use ieee.numeric_std.all;

entity fwd_unit is
    port(
        reg_s1 : in std_logic_vector(4 downto 0);
        reg_s2 : in std_logic_vector(4 downto 0);
        reg_dst : in std_logic_vector(4 downto 0);

        mem_wb_reg_dst : in std_logic_vector(4 downto 0);
        ex_mem_reg_dst : in std_logic_vector(4 downto 0);

        -- flags control ex/mem e mem/wb
        ex_mem_reg_w : in std_logic;
        mem_wb_reg_w : in std_logic;

        forward_a : out std_logic_vector(1 downto 0);
        forward_b : out std_logic_vector(1 downto 0);
        forward_c : out std_logic
    );
end fwd_unit;

architecture Behavioral of fwd_unit is
    begin
        forward_decode : process(reg_s1, reg_s2, reg_dst, mem_wb_reg_dst, ex_mem_reg_dst, ex_mem_reg_w, mem_wb_reg_w) is
            begin
            	 forward_a <= "00";
            	 forward_b <= "00";
            	 forward_c <= '0';
            	
                if (ex_mem_reg_w = '1') and (ex_mem_reg_dst /= "00000") then
                    if (ex_mem_reg_dst = reg_s1) then
                        forward_a <= "10";
                    end if;
                    if (ex_mem_reg_dst = reg_s2) then
                        forward_b <= "10";
                        forward_c <= '1';
                    end if;
                end if;
			 
                if (mem_wb_reg_w = '1') and (mem_wb_reg_dst /= "00000") and not (ex_mem_reg_w ='1' and (ex_mem_reg_dst /= "00000") and (ex_mem_reg_dst = reg_s1)) and (mem_wb_reg_dst = reg_s1) then
                    forward_a <= "01";
                end if;
                if (mem_wb_reg_w = '1') and (mem_wb_reg_dst /= "00000") and not (ex_mem_reg_w ='1' and (ex_mem_reg_dst /= "00000") and (ex_mem_reg_dst = reg_s2)) and (mem_wb_reg_dst = reg_s2) then
                    forward_b <= "01";
                end if;

        end process forward_decode;
end Behavioral;

// VHDL entity hzd_unit, as the project stores it:
library ieee;
use ieee.std_logic_1164.all;


entity hzd_unit is
    port(
        id_ex_mem_r : in std_logic;
        id_ex_reg_dst : in std_logic_vector(4 downto 0);
        if_id_reg_s1 : in std_logic_vector(4 downto 0);
        if_id_reg_s2 : in std_logic_vector(4 downto 0);

        pc_write : out std_logic;
        if_id_write : out std_logic;
        bubble : out std_logic
    );
end hzd_unit;

architecture Behavioral of hzd_unit is
    begin 

        hzd_detection: process(id_ex_mem_r, id_ex_reg_dst, if_id_reg_s1, if_id_reg_s2)
        begin 
            if (id_ex_mem_r = '1') then
                if (id_ex_reg_dst = if_id_reg_s1) or (id_ex_reg_dst = if_id_reg_s2) then -- stall
                    pc_write <= '0';
                    if_id_write <= '0';
                    bubble <= '1';
                end if;
            else
               pc_write <= '1';
            	if_id_write <= '1';
            	bubble <= '0';
            end if;
        end process hzd_detection;
end Behavioral;

// VHDL entity mem_br_taken, as the project stores it:
library ieee;
use ieee.std_logic_1164.all;

entity mem_br_taken is
    port (
        alu_br : in std_logic;
        branch : in std_logic;

        flush : out std_logic
    );
end mem_br_taken;

architecture Behavioral of mem_br_taken is
    begin
        process (alU_br, branch)
        begin
            if (alU_br = '1' and branch = '1') then
                flush <= '1';
            else flush <= '0';
            end if;
        end process;
end Behavioral;

// VHDL entity alu_simd, as the project stores it:
library ieee;
use ieee.std_logic_1164.all;
use ieee.numeric_std.all;

entity alu_simd is
	port(
		A_i, B_i  : in std_logic_vector(31 downto 0);
		instruction : in std_logic_vector(31 downto 0);
		S_o		 : out std_logic_vector(31 downto 0);

        opcode : in std_logic_vector(3 downto 0)
	);
end alu_simd;

architecture Behavioral of alu_simd is
	component CLA_4 is
		port(
			X : in std_logic_vector(3 downto 0);
			y : in std_logic_vector(3 downto 0);
			ci : in std_logic;
			co : out std_logic;
			z : out std_logic_vector(3 downto 0)
		);
	end component CLA_4;
	
	signal vecSize_i : std_logic_vector(2 downto 0) := (others => '0');
	signal A, B, saida8, saida4, saida2, saida1 : std_logic_vector(31 downto 0) := (others => '0');
	signal carrys : std_logic_vector(8 downto 0) := (others => '0'); -- sinal auxiliar 7 downto 0 = carrys, e carrys(0) sempre depende de mode_i
	
begin

	ints_8: for i in 0 to 7 generate
		adder0to7: CLA_4 port map(A(4*(i+1)-1 downto 4*i), B(4*(i+1)-1 downto 4*i), carrys(0), carrys(i+1), saida8(4*(i+1)-1 downto 4*i));
	end generate;

	-- to do: corrigir lógica
	ints_4: for i in 0 to 3 generate
		adder8to11: CLA_4 port map(A(4*(2*i+1)-1 downto 8*i), B(4*(i*2+1)-1 downto 8*i), carrys(0), carrys(2*i+1), saida4(4*(i*2+1)-1 downto 8*i));
		adder12to15: CLA_4 port map(A(4*(2*i+2)-1 downto 4*(i*2+1)), B(4*(2*i+2)-1 downto 4*(i*2+1)), carrys(2*i+1), carrys(2*i+2), saida4(4*(2*i+2)-1 downto 4*(i*2+1)));
	end generate;

	ints_2: for i in 0 to 1 generate
		adder16to17: CLA_4 port map(A(4*(4*i+1)-1 downto 16*i), B(4*(4*i+1)-1 downto 16*i), carrys(0), carrys(4*i+1), saida2(4*(4*i+1)-1 downto 16*i));
		adder18to19: CLA_4 port map(A(4*(4*i+2)-1 downto 4*(i*4+1)), B(4*(4*i+2)-1 downto 4*(i*4+1)), carrys(4*i+1), carrys(4*i+2), saida2(4*(4*i+2)-1 downto 4*(i*4+1)));
		adder20to21: CLA_4 port map(A(4*(4*i+3)-1 downto 4*(i*4+2)), B(4*(4*i+3)-1 downto 4*(i*4+2)), carrys(4*i+2), carrys(4*i+3), saida2(4*(4*i+3)-1 downto 4*(i*4+2)));
		adder22to23: CLA_4 port map(A(4*(4*i+4)-1 downto 4*(i*4+3)), B(4*(4*i+4)-1 downto 4*(i*4+3)), carrys(4*i+3), carrys(4*i+4), saida2(4*(4*i+4)-1 downto 4*(i*4+3)));
	end generate;

	ints_1: for i in 0 to 7 generate
		adder24to30: CLA_4 port map(A(4*(i+1)-1 downto 4*i), B(4*(i+1)-1 downto 4*i), carrys(i), carrys(i+1), saida1(4*(i+1)-1 downto 4*i));
	end generate;
	
	process(saida1, saida2, saida4, saida8, opcode, instruction) is
		begin
            if instruction(6 downto 0) = "1110011" or instruction(6 downto 0) = "0011011" or instruction(6 downto 0) = "0111011" then
                -- addi, slli, srli
                vecSize_i <= instruction(14 downto 12);
            else vecSize_i <= instruction(27 downto 25); -- add, sub, sll e srl
            end if;

            if opcode = "0001" then -- soma
                A <= A_i;
                B <= B_i;
                carrys(0) <= '0';
            elsif opcode = "0010" then -- sub
                A <= A_i;
                B <= not B_i;
                carrys(0) <= '1';

            elsif opcode = "0110" then -- shift left
                A <= A_i;
                B <= B_i;
                case vecSize_i is
                    when "000" => -- se 8 de 4 bits
                        if B(2 downto 0) >= "100" then
                            S_o <= (others => '0');
                        elsif B(2 downto 0) = "000" then
                            S_o <= A;
                        else
                            S_o(3 downto 0) <= std_logic_vector(shift_left(unsigned(A(3 downto 0)), to_integer(unsigned(B(2 downto 0)))));
                            S_o(7 downto 4) <= std_logic_vector(shift_left(unsigned(A(7 downto 4)), to_integer(unsigned(B(2 downto 0)))));
                            S_o(11 downto 8) <= std_logic_vector(shift_left(unsigned(A(11 downto 8)), to_integer(unsigned(B(2 downto 0)))));
                            S_o(15 downto 12) <= std_logic_vector(shift_left(unsigned(A(15 downto 12)), to_integer(unsigned(B(2 downto 0)))));
                            S_o(19 downto 16) <= std_logic_vector(shift_left(unsigned(A(19 downto 16)), to_integer(unsigned(B(2 downto 0)))));
                            S_o(23 downto 20) <= std_logic_vector(shift_left(unsigned(A(23 downto 20)), to_integer(unsigned(B(2 downto 0)))));
                            S_o(27 downto 24) <= std_logic_vector(shift_left(unsigned(A(27 downto 24)), to_integer(unsigned(B(2 downto 0)))));
                            S_o(31 downto 28) <= std_logic_vector(shift_left(unsigned(A(31 downto 28)), to_integer(unsigned(B(2 downto 0)))));
                        end if;
                    when "001" => -- se 4 de 8 bits
                        if B(3 downto 0) >= "1000" then
                            S_o <= (others => '0');
                        elsif B(3 downto 0) = "0000" then
                            S_o <= A;
                        else
                            S_o(7 downto 0) <= std_logic_vector(shift_left(unsigned(A(7 downto 0)), to_integer(unsigned(B(3 downto 0)))));
                            S_o(15 downto 8) <= std_logic_vector(shift_left(unsigned(A(15 downto 8)), to_integer(unsigned(B(3 downto 0)))));
                            S_o(23 downto 16) <= std_logic_vector(shift_left(unsigned(A(23 downto 16)), to_integer(unsigned(B(3 downto 0)))));
                            S_o(31 downto 24) <= std_logic_vector(shift_left(unsigned(A(31 downto 24)), to_integer(unsigned(B(3 downto 0)))));
                        end if;
                    when "010" => -- se 2 de 16 bits
                        if B(4 downto 0) >= "10000" then
                            S_o <= (others => '0');
                        elsif B(4 downto 0) = "00000" then
                            S_o <= A;
                        else
                            S_o(15 downto 0) <= std_logic_vector(shift_left(unsigned(A(15 downto 0)), to_integer(unsigned(B(4 downto 0)))));
                            S_o(31 downto 16) <= std_logic_vector(shift_left(unsigned(A(31 downto 16)), to_integer(unsigned(B(4 downto 0)))));
                        end if;
                    when "011" => -- se 1 de 32 bits
                        if B(5 downto 0) >= "100000" then
                            S_o <= (others => '0');
                        elsif B(5 downto 0) = "000000" then
                            S_o <= A;
                        else
                            S_o <= std_logic_vector(shift_left(unsigned(A), to_integer(unsigned(B(5 downto 0)))));
                        end if;
                    when others =>
                        S_o <= (others => 'Z');
                end case;
            
            elsif opcode = "0111" then -- shift right
                A <= A_i;
                B <= B_i;
                case vecSize_i is
                    when "000" => -- se 8 de 4 bits
                        if B(2 downto 0) >= "100" then
                            S_o <= (others => '0');
                        elsif B(2 downto 0) = "000" then
                            S_o <= A;
                        else
                            S_o(3 downto 0) <= std_logic_vector(shift_right(unsigned(A(3 downto 0)), to_integer(unsigned(B(2 downto 0)))));
                            S_o(7 downto 4) <= std_logic_vector(shift_right(unsigned(A(7 downto 4)), to_integer(unsigned(B(2 downto 0)))));
                            S_o(11 downto 8) <= std_logic_vector(shift_right(unsigned(A(11 downto 8)), to_integer(unsigned(B(2 downto 0)))));
                            S_o(15 downto 12) <= std_logic_vector(shift_right(unsigned(A(15 downto 12)), to_integer(unsigned(B(2 downto 0)))));
                            S_o(19 downto 16) <= std_logic_vector(shift_right(unsigned(A(19 downto 16)), to_integer(unsigned(B(2 downto 0)))));
                            S_o(23 downto 20) <= std_logic_vector(shift_right(unsigned(A(23 downto 20)), to_integer(unsigned(B(2 downto 0)))));
                            S_o(27 downto 24) <= std_logic_vector(shift_right(unsigned(A(27 downto 24)), to_integer(unsigned(B(2 downto 0)))));
                            S_o(31 downto 28) <= std_logic_vector(shift_right(unsigned(A(31 downto 28)), to_integer(unsigned(B(2 downto 0)))));
                        end if;
                    when "001" => -- se 4 de 8 bits
                        if B(3 downto 0) >= "1000" then
                            S_o <= (others => '0');
                        elsif B(3 downto 0) = "0000" then
                            S_o <= A;
                        else
                            S_o(7 downto 0) <= std_logic_vector(shift_right(unsigned(A(7 downto 0)), to_integer(unsigned(B(3 downto 0)))));
                            S_o(15 downto 8) <= std_logic_vector(shift_right(unsigned(A(15 downto 8)), to_integer(unsigned(B(3 downto 0)))));
                            S_o(23 downto 16) <= std_logic_vector(shift_right(unsigned(A(23 downto 16)), to_integer(unsigned(B(3 downto 0)))));
                            S_o(31 downto 24) <= std_logic_vector(shift_right(unsigned(A(31 downto 24)), to_integer(unsigned(B(3 downto 0)))));
                        end if;
                    when "010" => -- se 2 de 16 bits
                        if B(4 downto 0) >= "10000" then
                            S_o <= (others => '0');
                        elsif B(4 downto 0) = "00000" then
                            S_o <= A;
                        else
                            S_o(15 downto 0) <= std_logic_vector(shift_right(unsigned(A(15 downto 0)), to_integer(unsigned(B(4 downto 0)))));
                            S_o(31 downto 16) <= std_logic_vector(shift_right(unsigned(A(31 downto 16)), to_integer(unsigned(B(4 downto 0)))));
                        end if;
                    when "011" => -- se 1 de 32 bits
                        if B(5 downto 0) >= "100000" then
                            S_o <= (others => '0');
                        elsif B(5 downto 0) = "000000" then
                            S_o <= A;
                        else
                            S_o <= std_logic_vector(shift_right(unsigned(A), to_integer(unsigned(B(5 downto 0)))));
                        end if;
                    when others =>
                        S_o <= (others => 'Z');
                end case;
            else S_o <= (others => 'Z');
            end if;

            if opcode = "0001" or opcode = "0010" then
                case vecSize_i is
                    when "000" =>
                        S_o <= saida8;
                    when "001" =>
                        S_o <= saida4;
                    when "010" =>	
                        S_o <= saida2;
                    when "011" =>
                        S_o <= saida1;
                    when others =>
                        S_o <= (others => 'Z');
                end case;
            end if;
	end process;
end Behavioral;

// VHDL entity CLA_4, as the project stores it:
LIBRARY ieee;
USE ieee.std_logic_1164.all;

entity CLA_4 is
	port(
		X : in std_logic_vector(3 downto 0);
		Y : in std_logic_vector(3 downto 0);
		ci : in std_logic;
		co : out std_logic;
		z : out std_logic_vector(3 downto 0)
	);
end CLA_4;

-- nessa arquitetura, os sinais 'p' e 'g' são gerados em paralelo. Isso acelera ao máximo o processo de soma
architecture Behavioral of CLA_4 is
	signal p     : std_logic_vector(3 downto 0);
    signal g     : std_logic_vector(3 downto 0);
    signal carrys: std_logic_vector(4 downto 0);
	begin
		-- Gerar os sinais 'p' e 'g' em paralelo
		process(X, Y)
			variable p_temp : std_logic_vector(3 downto 0);
			variable g_temp : std_logic_vector(3 downto 0);
		begin
			for i in 0 to 3 loop
				p_temp(i) := X(i) xor Y(i);
				g_temp(i) := X(i) and Y(i);
			end loop;
			p <= p_temp;
			g <= g_temp;
		end process;
	
		-- Calcular os valores dos carrys em paralelo
		carrys(0) <= ci;
		carrys(1) <= g(0) or (p(0) and carrys(0));
		carrys(2) <= g(1) or (p(1) and carrys(1));
		carrys(3) <= g(2) or (p(2) and carrys(2));
		carrys(4) <= g(3) or (p(3) and carrys(3));
	
		-- Atribuir os valores dos sinais de saída
		co <= carrys(4);
		z <= X xor Y xor carrys(3 downto 0);
	end Behavioral;
